# Fritzing sketch pan tilt absolute (saved by Fritzing 0.8.7b)

parts:
  IC1 = RobotGeek Sensor Shield [chip_label=?]
  Part1 = RobotGeek Servo
  Part2 = RobotGeek Servo
  Part3 = RobotGeek Slider
  Part4 = RobotGeek Rotational Knob

nets:
  N1: IC1.pin22, IC1.pin23
  N2: IC1.pin26, IC1.pin27
  N3: IC1.pin28, Part1.connector0pin
  N4: IC1.pin29, Part1.connector1pin
  N5: IC1.pin30, Part1.connector2pin
  N6: IC1.pin31, Part2.connector0pin
  N7: IC1.pin32, Part2.connector1pin
  N8: IC1.pin33, Part2.connector2pin
  N9: IC1.pin64, Part3.connector1pin
  N10: IC1.pin65, Part3.connector2pin
  N11: IC1.pin66, Part3.connector0pin
  N12: IC1.pin76, Part4.connector1pin
  N13: IC1.pin77, Part4.connector2pin
  N14: IC1.pin78, Part4.connector0pin

custom parts:
  RobotGeek Slider: A linear potentiometer breakout board for the RobotGeek Sensor System
  RobotGeek Rotational Knob: A rotary potentiometer breakout board for the RobotGeek Sensor System
