# Fritzing sketch pan tilt incremental (saved by Fritzing 0.8.7b)

parts:
  IC1 = RobotGeek Sensor Shield [chip_label=?]
  Part1 = RobotGeek Servo
  Part2 = RobotGeek Servo
  j1 = RobotGeek Joystick
  j2 = RobotGeek Joystick

nets:
  N1: IC1.pin22, IC1.pin23
  N2: IC1.pin26, IC1.pin27
  N3: IC1.pin28, Part1.connector0pin
  N4: IC1.pin29, Part1.connector1pin
  N5: IC1.pin30, Part1.connector2pin
  N6: IC1.pin31, Part2.connector0pin
  N7: IC1.pin32, Part2.connector1pin
  N8: IC1.pin33, Part2.connector2pin
  N9: IC1.pin64, j2.pin5
  N10: IC1.pin65, j2.pin6
  N11: IC1.pin66, j2.pin4
  N12: IC1.pin76, j1.pin2
  N13: IC1.pin77, j1.pin3
  N14: IC1.pin78, j1.pin1
