# Fritzing sketch aquarium (saved by Fritzing 0.8.7b)

parts:
  IC1 = RobotGeek Sensor Shield [chip_label=?]
  Part2 = RobotGeek Pumping Station
  Part3 = RobotGeek LED Driver
  s1 = Float Switch

nets:
  N1: IC1.pin22, IC1.pin23
  N2: IC1.pin25, IC1.pin26
  N3: IC1.pin44, s1.pin1
  N4: IC1.pin45, s1.pin2
  N5: IC1.pin49, Part2.connector1pin
  N6: IC1.pin50, Part2.connector0pin
  N7: IC1.pin51, Part2.connector2pin
  N8: IC1.pin52, Part3.connector1pin
  N9: IC1.pin53, Part3.connector2pin
  N10: IC1.pin54, Part3.connector0pin

custom parts:
  RobotGeek Pumping Station: A pumping station comprised of a pushbutton, a RobotGeek relay, a liquid pump and a DC Jack
  RobotGeek LED Driver: A LED Driver breakout board for the RobotGeek Sensor System
  Float Switch: A simple float switch
