# Fritzing sketch lcd (saved by Fritzing 0.8.7b)

parts:
  U1 = RobotGeek LCD-16X2 [package=lcd-16x2]
  IC1 = RobotGeek Sensor Shield [chip_label=?]
  U2 = RobotGeek IIc LCD Backpack [chip_label=IC package="SIP (Single Inline) [THT]"]
  j1 = RobotGeek Joystick
  Part1 = RobotGeek Rotational Knob
  Part2 = RobotGeek Pushbutton

nets:
  N1: U1.VSS, U2.pin16
  N2: U1.VDD, U2.pin22
  N3: U1.VO, U2.pin21
  N4: U1.RS, U2.pin20
  N5: U1.R_W, U2.pin19
  N6: U1.E, U2.pin18
  N7: U1.DB0, U2.pin17
  N8: U1.DB1, U2.pin10
  N9: U1.DB2, U2.pin11
  N10: U1.DB3, U2.pin12
  N11: U1.DB4, U2.pin13
  N12: U1.DB5, U2.pin14
  N13: U1.DB6, U2.pin15
  N14: U1.DB7, U2.pin8
  N15: U1.A, U2.pin7
  N16: U1.K, U2.pin9
  N17: IC1.pin5, U2.pin3
  N18: IC1.pin6, U2.pin2
  N19: IC1.pin7, U2.pin4
  N20: IC1.pin8, U2.pin1
  N21: IC1.pin22, IC1.pin23
  N22: IC1.pin25, IC1.pin26
  N23: IC1.pin43, Part2.connector1pin
  N24: IC1.pin44, Part2.connector2pin
  N25: IC1.pin45, Part2.connector0pin
  N26: IC1.pin61, j1.pin5
  N27: IC1.pin62, j1.pin6
  N28: IC1.pin63, j1.pin4
  N29: IC1.pin64, j1.pin2
  N30: IC1.pin65, j1.pin3
  N31: IC1.pin66, j1.pin1
  N32: IC1.pin76, Part1.connector1pin
  N33: IC1.pin77, Part1.connector2pin
  N34: IC1.pin78, Part1.connector0pin

custom parts:
  RobotGeek LCD-16X2: White on blue LCD
  RobotGeek IIc LCD Backpack: Backpack for 16x2 LCD
  RobotGeek Rotational Knob: A rotary potentiometer breakout board for the RobotGeek Sensor System
  RobotGeek Pushbutton: A basic pushbutton breakout board for the RobotGeek Sensor System
