# Fritzing sketch night light (saved by Fritzing 0.8.7b)

parts:
  IC1 = RobotGeek Sensor Shield [chip_label=?]
  U1 = PowerSwitch Tail II
  U2 = SimplyTronics PIR Sensor

nets:
  N1: IC1.pin22, IC1.pin23
  N2: IC1.pin25, IC1.pin26
  N3: IC1.pin43, U2.pin3
  N4: IC1.pin44, U2.pin4
  N5: IC1.pin45, U2.pin2
  N6: IC1.pin50, U1.pin2
  N7: IC1.pin51, U1.pin1

custom parts:
  PowerSwitch Tail II: Relay connected to 120v us power cord
  SimplyTronics PIR Sensor: PIR Motion sensor
