# Fritzing sketch servo button (saved by Fritzing 0.8.7b)

parts:
  IC1 = RobotGeek Sensor Shield [chip_label=?]
  Part1 = RobotGeek Servo
  Part2 = RobotGeek Pushbutton
  Part3 = RobotGeek Pushbutton
  Part4 = RobotGeek Pushbutton

nets:
  N1: IC1.pin22, IC1.pin23
  N2: IC1.pin26, IC1.pin27
  N3: IC1.pin28, Part1.connector0pin
  N4: IC1.pin29, Part1.connector1pin
  N5: IC1.pin30, Part1.connector2pin
  N6: IC1.pin43, Part2.connector1pin
  N7: IC1.pin44, Part2.connector2pin
  N8: IC1.pin45, Part2.connector0pin
  N9: IC1.pin49, Part3.connector1pin
  N10: IC1.pin50, Part3.connector2pin
  N11: IC1.pin51, Part3.connector0pin
  N12: IC1.pin52, Part4.connector1pin
  N13: IC1.pin53, Part4.connector2pin
  N14: IC1.pin54, Part4.connector0pin

custom parts:
  RobotGeek Pushbutton: A basic pushbutton breakout board for the RobotGeek Sensor System
