# Fritzing sketch shotBot (saved by Fritzing 0.8.7b)

parts:
  Part2 = RobotGeek Pushbutton
  Part3 = RobotGeek Pushbutton
  IC1 = RobotGeek Sensor Shield [chip_label=?]
  Part4 = RobotGeek Pumping Station
  Part5 = RobotGeek Pumping Station

nets:
  N1: Part2.connector0pin, IC1.pin54
  N2: Part2.connector1pin, IC1.pin52
  N3: Part2.connector2pin, IC1.pin53
  N4: Part3.connector0pin, IC1.pin57
  N5: Part3.connector1pin, IC1.pin55
  N6: Part3.connector2pin, IC1.pin56
  N7: IC1.pin22, IC1.pin23
  N8: IC1.pin25, IC1.pin26
  N9: IC1.pin43, Part4.connector1pin
  N10: IC1.pin44, Part4.connector0pin
  N11: IC1.pin45, Part4.connector2pin
  N12: IC1.pin49, Part5.connector1pin
  N13: IC1.pin50, Part5.connector0pin
  N14: IC1.pin51, Part5.connector2pin

custom parts:
  RobotGeek Pushbutton: A basic pushbutton breakout board for the RobotGeek Sensor System
  RobotGeek Pumping Station: A pumping station comprised of a pushbutton, a RobotGeek relay, a liquid pump and a DC Jack
