# Fritzing sketch single RG servo button (saved by Fritzing 0.8.7b)

parts:
  IC1 = RobotGeek Sensor Shield [chip_label=?]
  Part1 = RobotGeek Servo
  S1 = Round Pushbutton

nets:
  N1: IC1.pin22, IC1.pin23
  N2: IC1.pin26, IC1.pin27
  N3: IC1.pin28, Part1.connector0pin
  N4: IC1.pin29, Part1.connector1pin
  N5: IC1.pin30, Part1.connector2pin
  N6: IC1.pin44, S1.leg1
  N7: IC1.pin45, S1.leg0
