# Fritzing sketch snapperArmBackhoe (saved by Fritzing 0.8.7b)

parts:
  IC1 = RobotGeek Sensor Shield [chip_label=?]
  Part6 = 9g Servo
  Part7 = RobotGeek Servo
  Part8 = RobotGeek Servo
  Part9 = RobotGeek Servo
  Part10 = RobotGeek Servo
  S1 = RobotGeek 6v 2a Power Supply [package=THT]  # not connected
  j1 = RobotGeek Joystick
  Part11 = RobotGeek Pushbutton
  Part12 = RobotGeek Pushbutton
  Part13 = RobotGeek Rotational Knob
  j2 = RobotGeek Joystick
  j3 = RobotGeek Joystick

nets:
  N1: IC1.pin13, Part10.connector0pin
  N2: IC1.pin14, Part10.connector1pin
  N3: IC1.pin15, Part10.connector2pin
  N4: IC1.pin16, Part9.connector0pin
  N5: IC1.pin17, Part9.connector1pin
  N6: IC1.pin18, Part9.connector2pin
  N7: IC1.pin19, Part7.connector0pin
  N8: IC1.pin20, Part7.connector1pin
  N9: IC1.pin21, Part7.connector2pin
  N10: IC1.pin23, IC1.pin24
  N11: IC1.pin26, IC1.pin27
  N12: IC1.pin28, Part8.connector0pin
  N13: IC1.pin29, Part8.connector1pin
  N14: IC1.pin30, Part8.connector2pin
  N15: IC1.pin31, Part6.connector0pin
  N16: IC1.pin32, Part6.connector1pin
  N17: IC1.pin33, Part6.connector2pin
  N18: IC1.pin43, Part11.connector1pin
  N19: IC1.pin44, Part11.connector2pin
  N20: IC1.pin45, Part11.connector0pin
  N21: IC1.pin49, Part12.connector1pin
  N22: IC1.pin50, Part12.connector2pin
  N23: IC1.pin51, Part12.connector0pin
  N24: IC1.pin61, j1.pin2
  N25: IC1.pin62, j1.pin3
  N26: IC1.pin63, j1.pin1
  N27: IC1.pin64, j3.pin2
  N28: IC1.pin65, j3.pin3
  N29: IC1.pin66, j3.pin1
  N30: IC1.pin67, j2.pin2
  N31: IC1.pin68, j2.pin3
  N32: IC1.pin69, j2.pin1
  N33: IC1.pin70, Part13.connector1pin
  N34: IC1.pin71, Part13.connector2pin
  N35: IC1.pin72, Part13.connector0pin
  N36: IC1.pin76, j3.pin5
  N37: IC1.pin77, j3.pin6
  N38: IC1.pin78, j3.pin4

custom parts:
  9g Servo: 9g servo
  RobotGeek 6v 2a Power Supply: A generic pushbutton.
  RobotGeek Joystick: RobotGeek Joystick - stick connector
  RobotGeek Pushbutton: A basic pushbutton breakout board for the RobotGeek Sensor System
  RobotGeek Rotational Knob: A rotary potentiometer breakout board for the RobotGeek Sensor System
