# Fritzing sketch snapperSequence (saved by Fritzing 0.8.7b)

parts:
  IC1 = RobotGeek Sensor Shield [chip_label=?]
  Part6 = 9g Servo
  Part7 = RobotGeek Servo
  Part8 = RobotGeek Servo
  Part9 = RobotGeek Servo
  Part10 = RobotGeek Servo
  S1 = RobotGeek 6v 2a Power Supply [package=THT]  # not connected
  Part11 = RobotGeek Pushbutton

nets:
  N1: IC1.pin13, Part10.connector0pin
  N2: IC1.pin14, Part10.connector1pin
  N3: IC1.pin15, Part10.connector2pin
  N4: IC1.pin16, Part9.connector0pin
  N5: IC1.pin17, Part9.connector1pin
  N6: IC1.pin18, Part9.connector2pin
  N7: IC1.pin19, Part7.connector0pin
  N8: IC1.pin20, Part7.connector1pin
  N9: IC1.pin21, Part7.connector2pin
  N10: IC1.pin23, IC1.pin24
  N11: IC1.pin26, IC1.pin27
  N12: IC1.pin28, Part8.connector0pin
  N13: IC1.pin29, Part8.connector1pin
  N14: IC1.pin30, Part8.connector2pin
  N15: IC1.pin31, Part6.connector0pin
  N16: IC1.pin32, Part6.connector1pin
  N17: IC1.pin33, Part6.connector2pin
  N18: IC1.pin43, Part11.connector1pin
  N19: IC1.pin44, Part11.connector2pin
  N20: IC1.pin45, Part11.connector0pin

custom parts:
  9g Servo: 9g servo
  RobotGeek 6v 2a Power Supply: A generic pushbutton.
  RobotGeek Pushbutton: A basic pushbutton breakout board for the RobotGeek Sensor System
