# Fritzing sketch sump pump (saved by Fritzing 0.8.7b)

parts:
  IC1 = RobotGeek Sensor Shield [chip_label=?]
  s1 = Float Switch
  U1 = PowerSwitch Tail II
  LED1 = LED - 5mm [color="Red (633nm)" package="5 mm [THT]"]  # not connected
  L1 = RobotGeek LED Driver

nets:
  N1: IC1.pin22, IC1.pin23
  N2: IC1.pin25, IC1.pin26
  N3: IC1.pin44, s1.pin2
  N4: IC1.pin45, s1.pin1
  N5: IC1.pin50, U1.pin2
  N6: IC1.pin51, U1.pin1
  N7: IC1.pin52, L1.pin2
  N8: IC1.pin53, L1.pin3
  N9: IC1.pin54, L1.pin1

custom parts:
  Float Switch: A simple float switch
  PowerSwitch Tail II: Relay connected to 120v us power cord
  RobotGeek LED Driver: Transistor based LED Driver compatible with the RobotGeek Sensor System
